// Logisim project ex1.circ as structural Verilog: 6 circuits, main circuit AND2
module AND2 (
  input  A,
  input  B,
  output RESULT
);

  and and_1 (RESULT, A, B);

  // Notes on the sheet:
  //   Sample Circuit
endmodule

module NAND2 (
  input  A,
  input  B,
  output RESULT
);

  wire and_1_out;

  and and_1 (and_1_out, A, B);
  not not_1 (RESULT, and_1_out);
endmodule

module NOR2 (
  input  A,
  input  B,
  output RESULT
);

  wire or_1_out;

  or or_1 (or_1_out, A, B);
  not not_1 (RESULT, or_1_out);
endmodule

module XOR2 (
  input  A,
  input  B,
  output RESULT
);

  wire nand2_1_result, or_1_out;

  or or_1 (or_1_out, B, A);
  NAND2 nand2_1 (.A(A), .B(B), .RESULT(nand2_1_result));
  and and_1 (RESULT, nand2_1_result, or_1_out);
endmodule

module MUX2 (
  input  A,
  input  B,
  input  SEL,
  output RESULT
);

  wire and_1_out, and_2_out, xor2_1_result;

  and and_1 (and_1_out, A, SEL);
  XOR2 xor2_1 (.A(B), .B(SEL), .RESULT(xor2_1_result));
  and and_2 (and_2_out, B, xor2_1_result);
  or or_1 (RESULT, and_1_out, and_2_out);
endmodule

module MUX4 (
  input  SEL1,
  input  SEL0,
  input  A,
  input  B,
  input  C,
  input  D,
  output RESULT
);

  wire and_1_out, and_2_out, and_3_out, and_4_out, not_1_out, not_2_out, not_3_out, not_4_out;

  not not_1 (not_1_out, SEL1);
  not not_2 (not_2_out, SEL0);
  not not_3 (not_3_out, SEL1);
  not not_4 (not_4_out, SEL0);
  and and_1 (and_1_out, A, not_1_out, not_2_out);
  and and_2 (and_2_out, B, not_3_out, SEL0);
  and and_3 (and_3_out, C, SEL1, not_4_out);
  and and_4 (and_4_out, D, SEL1, SEL0);
  or or_1 (RESULT, and_1_out, and_2_out, and_3_out, and_4_out);
endmodule
