// Logisim project ex5.circ as structural Verilog: 2 circuits, main circuit main
module main (
  input  A,
  input  B,
  input  C,
  output Result
);

  wire and_1_out, and_2_out, and_3_out;

  and and_1 (and_1_out, B, C);
  and and_2 (and_2_out, ~A, ~B, ~C);  // AND_Gate
  and and_3 (and_3_out, B, ~C);  // AND_Gate
  or or_1 (Result, and_1_out, and_2_out, and_3_out);
endmodule

module simplier (
  input  A,
  input  B,
  input  C,
  output Result
);

  wire and_1_out;

  and and_1 (and_1_out, ~A, ~C);  // AND_Gate
  or or_1 (Result, and_1_out, B);
endmodule
