// Logisim project ex6.circ as structural Verilog: 8 circuits, main circuit main
module main (
  input  [3:0] in_1
);

  wire sa_1_out_2, sb_1_out_2, sc_1_out_2, sd_1_out_2, se_1_out_2, sf_1_out_2, sg_1_out_2;

  Sa sa_1 (.in_1(in_1), .out_2(sa_1_out_2));
  Sb sb_1 (.in_1(in_1), .out_2(sb_1_out_2));
  Sc sc_1 (.in_1(in_1), .out_2(sc_1_out_2));
  Sd sd_1 (.in_1(in_1), .out_2(sd_1_out_2));
  _7_Segment_Display u_7_segment_display_1 (
    .g(sg_1_out_2), .f(sf_1_out_2), .a(sa_1_out_2), .b(sb_1_out_2), .e(se_1_out_2), .d(sd_1_out_2),
    .c(sc_1_out_2));  // open: dp
  Se se_1 (.in_1(in_1), .out_2(se_1_out_2));
  Sf sf_1 (.in_1(in_1), .out_2(sf_1_out_2));
  Sg sg_1 (.in_1(in_1), .out_2(sg_1_out_2));
endmodule

module Sa (
  input  [3:0] in_1,
  output out_2
);

  wire and_1_out, and_2_out, and_3_out, and_4_out;

  and and_1 (and_1_out, ~in_1[3], in_1[1]);  // AND_Gate
  and and_2 (and_2_out, ~in_1[3], in_1[2], in_1[0]);  // AND_Gate
  or or_1 (out_2, and_1_out, and_2_out, and_3_out, and_4_out);
  and and_3 (and_3_out, in_1[3], ~in_1[2], ~in_1[1]);  // AND_Gate
  and and_4 (and_4_out, ~in_1[2], ~in_1[1], ~in_1[0]);  // AND_Gate
endmodule

module Sb (
  input  [3:0] in_1,
  output out_2
);

  wire and_1_out, and_2_out, and_3_out, and_4_out;

  and and_1 (and_1_out, ~in_1[3], ~in_1[2]);  // AND_Gate
  and and_2 (and_2_out, ~in_1[2], ~in_1[1]);  // AND_Gate
  or or_1 (out_2, and_1_out, and_2_out, and_3_out, and_4_out);
  and and_3 (and_3_out, ~in_1[3], in_1[0], in_1[1]);  // AND_Gate
  and and_4 (and_4_out, ~in_1[3], ~in_1[1], ~in_1[0]);  // AND_Gate
endmodule

module Sc (
  input  [3:0] in_1,
  output out_2
);

  wire and_1_out, and_2_out, and_3_out;

  and and_1 (and_1_out, ~in_1[3], in_1[2]);  // AND_Gate
  and and_2 (and_2_out, ~in_1[2], ~in_1[1]);  // AND_Gate
  or or_1 (out_2, and_1_out, and_2_out, and_3_out);
  and and_3 (and_3_out, in_1[0], ~in_1[3], in_1[1]);  // AND_Gate
endmodule

module Sd (
  input  [3:0] in_1,
  output out_2
);

  wire and_1_out, and_2_out, and_3_out, and_4_out;

  and and_1 (and_1_out, ~in_1[0], ~in_1[2], ~in_1[1]);  // AND_Gate
  and and_2 (and_2_out, ~in_1[3], in_1[2], ~in_1[1], in_1[0]);  // AND_Gate
  or or_1 (out_2, and_1_out, and_2_out, and_3_out, and_4_out);
  and and_3 (and_3_out, ~in_1[3], ~in_1[2], in_1[1]);  // AND_Gate
  and and_4 (and_4_out, ~in_1[3], in_1[1], ~in_1[0]);  // AND_Gate
endmodule

module Se (
  input  [3:0] in_1,
  output out_2
);

  wire and_1_out, and_2_out;

  and and_1 (and_1_out, ~in_1[2], ~in_1[0], ~in_1[1]);  // AND_Gate
  and and_2 (and_2_out, ~in_1[3], in_1[1], ~in_1[0]);  // AND_Gate
  or or_1 (out_2, and_1_out, and_2_out);
endmodule

module Sf (
  input  [3:0] in_1,
  output out_2
);

  wire and_1_out, and_2_out, and_3_out, and_4_out;

  and and_1 (and_1_out, ~in_1[3], ~in_1[1], ~in_1[0]);  // AND_Gate
  and and_2 (and_2_out, ~in_1[0], ~in_1[3], in_1[2]);  // AND_Gate
  or or_1 (out_2, and_1_out, and_2_out, and_3_out, and_4_out);
  and and_3 (and_3_out, in_1[3], ~in_1[2], ~in_1[1]);  // AND_Gate
  and and_4 (and_4_out, ~in_1[3], in_1[2], ~in_1[1]);  // AND_Gate
endmodule

module Sg (
  input  [3:0] in_1,
  output out_2
);

  wire and_1_out, and_2_out, and_3_out, and_4_out;

  and and_1 (and_1_out, ~in_1[3], in_1[2], ~in_1[1]);  // AND_Gate
  and and_2 (and_2_out, in_1[3], ~in_1[2], ~in_1[1]);  // AND_Gate
  or or_1 (out_2, and_1_out, and_2_out, and_3_out, and_4_out);
  and and_3 (and_3_out, ~in_1[3], ~in_1[2], in_1[1]);  // AND_Gate
  and and_4 (and_4_out, ~in_1[3], in_1[1], ~in_1[0]);  // AND_Gate
endmodule
